# Fritzing sketch Minitel Bridge (saved by Fritzing 1.0.4)
circuit board: 8.5cm x 2.5cm
breadboards: 1

parts:
  R1 = Resistor [tolerance=±5% power=0.25W resistance=220k package=THT]
  Minitel_DIN = DIN-5 jack (MIDI) [part_number=DC-205 package=THT]
  M1 = Arduino NANO RP2040 CONNECT with headers
  J1 = female pin header, 15 pins [form="♀ (female)"]
  J2 = female pin header, 15 pins [form="♀ (female)"]

nets:
  N1: R1.Pin_0, M1.+3V3, J1.pin14
  N2: R1.Pin_1, Minitel_DIN.3, M1.RX, J2.pin2
  N3: Minitel_DIN.2, M1.GND-4, M1.GND-29, J1.pin2, J2.pin4
  N4: Minitel_DIN.1, M1.TX, J2.pin1
  N5: M1.RESET-3, J2.pin3
  N6: M1.D2, J2.pin5
  N7: M1.D3, J2.pin6
  N8: M1.D4, J2.pin7
  N9: M1.D5, J2.pin8
  N10: M1.D6, J2.pin9
  N11: M1.D7, J2.pin10
  N12: M1.D8, J2.pin11
  N13: M1.D9, J2.pin12
  N14: M1.D10, J2.pin13
  N15: M1.D11, J2.pin14
  N16: M1.D12, J2.pin15
  N17: M1.D13, J1.pin15
  N18: M1.AREF, J1.pin13
  N19: M1.D14, J1.pin12
  N20: M1.D15, J1.pin11
  N21: M1.D16, J1.pin10
  N22: M1.D17, J1.pin9
  N23: M1.D18, J1.pin8
  N24: M1.D19, J1.pin7
  N25: M1.D20, J1.pin6
  N26: M1.D27, J1.pin5
  N27: M1.+5V, J1.pin4
  N28: M1.RESET-28, J1.pin3
  N29: M1.VIN, J1.pin1

notes:
  Minitel Bridge
  @Xenoth
